# Fritzing sketch quadstepper (saved by Fritzing 0.9.2b)
perfboards: 1

parts:
  M4 = Stepper Motor - Bipolar
  J2 = screw terminal, 4 pins
  U6 = mystery part, 28 pins [chip_label="A4983 stepper driver"]
  J3 = Screw terminal - 2 pins [package=THT]
  Part2 = Arduino Mega 2560 (Rev3)
  S2 = Pushbutton [package=THT]
  LED1 = LED - 3mm [color="Green (555nm)" package="3 mm [THT]"]  # not connected
  LED2 = LED - 3mm [color="Red (633nm)" package="3 mm [THT]"]  # not connected
  R1 = Resistor [tolerance=±5% resistance=220 package=THT]  # not connected
  R3 = Resistor [tolerance=±5% resistance=220 package=THT]  # not connected
  U7 = RJ45 Jack [package=rj45-8]
  U8 = RJ45 Jack [package=rj45-8]
  J4 = screw terminal, 2 pins

nets:
  N1: M4.C, J2.pin2, U6.pin19
  N2: J2.pin1, U6.pin20
  N3: J2.pin3, U6.pin18
  N4: J2.pin4, U6.pin17
  N5: U6.pin2, U6.pin3
  N6: U6.pin13, U7.7
  N7: U6.pin14, U7.8
  N8: U6.pin22, J4.pin2
  N9: J3.pin1, S2.leg1
  N10: J3.pin2, S2.leg0
  N11: Part2.5V, U8.4
  N12: Part2.D23, U8.8
  N13: Part2.D25, U8.7
  N14: Part2.D27, U8.6
  N15: Part2.GND, U8.5

notes:
  power supply
  8-35V & 2AMP
  (make sure input voltate is 100-250v / enclosed power supply unit)
  STEP
  DIR
  SWITCH
  GND
  5V
  (5pins)
  power LED
  blocked LED
  safety pushbutton
  SINGLE MODULE COMPONENTS
  28 pin socket
  x4 2pin screw terminals
  x2 5pin connector
