# Fritzing sketch installation-setup (saved by Fritzing 0.9.2b)
stripboards: 1

parts:
  Part1 = Arduino Uno (Rev3)
  S1 = Toggle Switch [package=THT]
  U1 = RJ45 Jack [package=rj45-8]
  U2 = RJ45 Jack [package=rj45-8]
  U3 = RJ45 Jack [package=rj45-8]
  U4 = RJ45 Jack [package=rj45-8]
  C1 = Electrolytic Capacitor [capacitance=0.1mF package="100 mil [THT, electrolytic]"]

nets:
  N1: Part1.A0, U1.4, U2.4, U3.4, U4.4
  N2: Part1.D8, U3.1
  N3: Part1.D9_PWM, U3.2
  N4: Part1.D10_PWM/SS, U3.6
  N5: Part1.D11_PWM/MOSI, U4.1
  N6: Part1.D12/MISO, U4.2
  N7: Part1.D13/SCK, U4.6
  N8: Part1.D2, U1.1
  N9: Part1.D3_PWM, U1.2
  N10: Part1.D4, U1.6
  N11: Part1.D5_PWM, U2.1
  N12: Part1.D6_PWM, U2.2
  N13: Part1.D7, U2.6
  N14: Part1.RESET, S1.COM
  N15: Part1.5V, U1.7, U2.7, U3.7, U4.7
  N16: Part1.GND, U1.8, U2.8, U3.8, U4.8, C1.-
  N17: S1.L1, C1.+
